# Fritzing sketch JJM_BioSynth_3-1 (saved by Fritzing 1.0.2b)
breadboards: 1

parts:
  R1 = Resistor [tolerance=±5% power=0.25W resistance=1M package=THT]
  U2 = LM 358 Dual Op-Amp [mn=TLV2462CP package="DIP8 [THT]"]
  C3 = Electrolytic Capacitor [capacitance=47µF voltage=50V package="100 mil [THT, electrolytic]"]
  R8 = Resistor [tolerance=±5% power=0.25W resistance=1.5k package=THT]
  C4 = Electrolytic Capacitor [capacitance=47µF voltage=35V package="100 mil [THT, electrolytic]"]
  C5 = Electrolytic Capacitor [capacitance=47µF voltage=35V package="100 mil [THT, electrolytic]"]
  R9 = Resistor [tolerance=±5% power=0.25W resistance=1M package=THT]
  C6 = Ceramic Capacitor [capacitance=10nF voltage=35V package="100 mil [THT, multilayer]"]
  R10 = Resistor [tolerance=±5% power=0.25W resistance=10k package=THT]
  C7 = Electrolytic Capacitor [capacitance=0.1mF voltage=35V package="100 mil [THT, electrolytic]"]
  U3 = ESP32S-HiLetgo [part_number=ESP32S-HiLetgo]
  C8 = Electrolytic Capacitor [capacitance=1µF voltage=35V package="100 mil [THT, electrolytic]"]
  C9 = Electrolytic Capacitor [capacitance=47µF voltage=35V package="100 mil [THT, electrolytic]"]

nets:
  ECG Black/GND: R1.Pin_0, U2.connector3, C3.-, R8.Pin_0, C4.-, C5.-, C7.-, U3.GND, C8.-, C9.-
  GSR 2: R1.Pin_1, U2.connector4
  A3: U2.connector0, R9.Pin_1, C6.0, U3.GPIO39
  N1: U2.connector1, R9.Pin_0, C6.1, R10.Pin_1
  Therm 2: U2.connector2, R8.Pin_1
  A0: U2.connector5, U2.connector6, U3.GPIO36
  3.3V/ECG Red/GSR 1/Therm 1: U2.connector7, C3.+, C4.+, C5.+, U3.3.3, C8.+, C9.+
  N2: R10.Pin_0, C7.+
  ECG Purple: U3.GPIO34

custom parts:
  ESP32S-HiLetgo: HiLetgo ESP-WROOM-32 ESP32 ESP-32S Development Board 2.4GHz Dual-Mode WiFi + Bluetooth Dual Cores Microcontroller The ESP32 integrated with Antenna switches, RF Balun, power amplifiers, low-noise amplifiers, filters, and management modules, and the entire solution occupies the least area of PCB. 2.4 GHz Wi-Fi plus Bluetooth dual-mode chip, with TSMC Ultra-low power consumption 40nm technology,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
